// Digital circuit Subtrator_8Bits.dig as structural Verilog
module Subtrator_8Bits (
  input  [7:0] A,
  input  [7:0] B,
  output [7:0] S
);

  wire subtrator_1bit_1_cout, subtrator_1bit_2_cout, subtrator_1bit_3_cout, subtrator_1bit_4_cout,
       subtrator_1bit_5_cout, subtrator_1bit_6_cout, subtrator_1bit_7_cout, subtrator_1bit_8_cout;

  Subtrator_1bit subtrator_1bit_1 (.a(A[0]), .b(B[0]), .Cin(1'b0), .S(S[0]), .Cout(subtrator_1bit_1_cout));
  Subtrator_1bit subtrator_1bit_2 (
    .a(A[1]), .b(B[1]), .Cin(subtrator_1bit_1_cout), .S(S[1]), .Cout(subtrator_1bit_2_cout));
  Subtrator_1bit subtrator_1bit_3 (
    .a(A[2]), .b(B[2]), .Cin(subtrator_1bit_2_cout), .S(S[2]), .Cout(subtrator_1bit_3_cout));
  Subtrator_1bit subtrator_1bit_4 (
    .a(A[3]), .b(B[3]), .Cin(subtrator_1bit_3_cout), .S(S[3]), .Cout(subtrator_1bit_4_cout));
  Subtrator_1bit subtrator_1bit_5 (
    .a(A[4]), .b(B[4]), .Cin(subtrator_1bit_4_cout), .S(S[4]), .Cout(subtrator_1bit_5_cout));
  Subtrator_1bit subtrator_1bit_6 (
    .a(A[5]), .b(B[5]), .Cin(subtrator_1bit_5_cout), .S(S[5]), .Cout(subtrator_1bit_6_cout));
  Subtrator_1bit subtrator_1bit_7 (
    .a(A[6]), .b(B[6]), .Cin(subtrator_1bit_6_cout), .S(S[6]), .Cout(subtrator_1bit_7_cout));
  Subtrator_1bit subtrator_1bit_8 (
    .a(A[7]), .b(B[7]), .Cin(subtrator_1bit_7_cout), .S(S[7]), .Cout(subtrator_1bit_8_cout));
  // also tied to GND on the sheet: subtrator_1bit_8_cout

  // Other names for the same wires on the sheet: A2 = A[1]; A4 = A[2]; A8 = A[3]; A16 = A[4]; A32 = A[5]; A64 = A[6];
  //   A128 = A[7]; B2 = B[1]; B4 = B[2]; B8 = B[3]; B16 = B[4]; B32 = B[5]; B64 = B[6]; B128 = B[7]; S2 = S[1];
  //   S4 = S[2]; S8 = S[3]; S16 = S[4]; S32 = S[5]; S64 = S[6]; S128 = S[7]
endmodule
