// Digital circuit multiplicador_8Bits.dig as structural Verilog
module multiplicador_8Bits (
  input  A0,
  input  B0,
  input  A1,
  input  A2,
  input  A3,
  input  A4,
  input  A5,
  input  A6,
  input  A7,
  input  B1,
  input  B2,
  input  B3,
  input  B4,
  input  B5,
  input  B6,
  input  B7,
  output P0,
  output P1,
  output P2,
  output P3,
  output P4,
  output P5,
  output P6,
  output P7,
  output P8,
  output P9,
  output P10,
  output P11,
  output P12,
  output P13,
  output P14,
  output P15
);

  wire and_1_out, and_2_out, and_3_out, and_4_out, and_5_out, and_6_out, and_7_out, and_8_out, and_9_out,
       and_10_out, and_11_out, and_12_out, and_13_out, and_14_out, and_15_out, and_16_out, and_17_out,
       and_18_out, and_19_out, and_20_out, and_21_out, and_22_out, and_23_out, and_24_out, and_25_out,
       and_26_out, and_27_out, and_28_out, and_29_out, and_30_out, and_31_out, and_32_out, and_33_out,
       and_34_out, and_35_out, and_36_out, and_37_out, and_38_out, and_39_out, and_40_out, and_41_out,
       and_42_out, and_43_out, and_44_out, and_45_out, and_46_out, and_47_out, and_48_out, and_49_out,
       and_50_out, and_51_out, and_52_out, and_53_out, and_54_out, and_55_out, and_56_out, and_57_out,
       and_58_out, and_59_out, and_60_out, and_61_out, and_62_out, and_63_out, full_adder_2_cout,
       full_adder_2_s, full_adder_3_cout, full_adder_4_cout, full_adder_4_s, full_adder_5_cout,
       full_adder_5_s, full_adder_6_cout, full_adder_7_cout, full_adder_7_s, full_adder_8_cout,
       full_adder_9_cout, full_adder_9_s, full_adder_10_cout, full_adder_10_s, full_adder_11_cout,
       full_adder_12_cout, full_adder_12_s, full_adder_13_cout, full_adder_13_s, full_adder_14_cout,
       full_adder_14_s, full_adder_15_cout, full_adder_15_s, full_adder_16_cout, full_adder_17_cout,
       full_adder_17_s, full_adder_18_cout, full_adder_18_s, full_adder_19_cout, full_adder_19_s,
       full_adder_20_cout, full_adder_20_s, full_adder_21_cout, full_adder_21_s, full_adder_22_cout,
       full_adder_22_s, full_adder_23_cout, full_adder_23_s, full_adder_24_cout, full_adder_24_s,
       full_adder_25_cout, full_adder_26_cout, full_adder_26_s, full_adder_27_cout, full_adder_27_s,
       full_adder_28_cout, full_adder_28_s, full_adder_29_cout, full_adder_29_s, full_adder_30_cout,
       full_adder_30_s, full_adder_31_cout, full_adder_31_s, full_adder_32_cout, full_adder_32_s,
       full_adder_33_cout, full_adder_33_s, full_adder_34_cout, full_adder_34_s, full_adder_35_cout,
       full_adder_35_s, full_adder_36_cout, full_adder_36_s, full_adder_37_cout, full_adder_37_s,
       full_adder_38_cout, full_adder_38_s, full_adder_39_cout, full_adder_39_s, full_adder_40_cout,
       full_adder_40_s, full_adder_41_cout, full_adder_41_s, full_adder_42_cout, full_adder_42_s,
       full_adder_43_cout, full_adder_43_s, full_adder_44_cout, full_adder_44_s, full_adder_45_cout,
       full_adder_45_s, full_adder_46_cout, full_adder_46_s, full_adder_47_cout, full_adder_47_s,
       full_adder_48_cout, full_adder_48_s, half_adder_1_cout, half_adder_1_s, half_adder_2_cout,
       half_adder_3_cout, half_adder_4_cout, half_adder_5_cout, half_adder_6_cout, half_adder_7_cout,
       half_adder_8_cout;

  and and_1 (and_1_out, A7, B7);
  full_adder full_adder_1 (.a(full_adder_2_cout), .b(and_1_out), .Cin(full_adder_3_cout), .S(P14), .Cout(P15));
  and and_2 (and_2_out, A7, B6);
  and and_3 (and_3_out, A6, B7);
  full_adder full_adder_2 (
    .a(full_adder_4_cout), .b(and_2_out), .Cin(full_adder_5_cout), .S(full_adder_2_s),
    .Cout(full_adder_2_cout));
  full_adder full_adder_3 (
    .a(full_adder_2_s), .b(and_3_out), .Cin(full_adder_6_cout), .S(P13), .Cout(full_adder_3_cout));
  and and_4 (and_4_out, A5, B7);
  and and_5 (and_5_out, A7, B5);
  full_adder full_adder_4 (
    .a(full_adder_9_cout), .b(and_5_out), .Cin(full_adder_10_cout), .S(full_adder_4_s),
    .Cout(full_adder_4_cout));
  and and_6 (and_6_out, A6, B6);
  full_adder full_adder_5 (
    .a(full_adder_4_s), .b(and_6_out), .Cin(full_adder_7_cout), .S(full_adder_5_s), .Cout(full_adder_5_cout));
  full_adder full_adder_6 (
    .a(full_adder_5_s), .b(and_4_out), .Cin(full_adder_8_cout), .S(P12), .Cout(full_adder_6_cout));
  and and_7 (and_7_out, A4, B7);
  and and_8 (and_8_out, A7, B4);
  and and_9 (and_9_out, A6, B5);
  and and_10 (and_10_out, A5, B6);
  full_adder full_adder_7 (
    .a(full_adder_10_s), .b(and_10_out), .Cin(full_adder_15_cout), .S(full_adder_7_s),
    .Cout(full_adder_7_cout));
  full_adder full_adder_8 (
    .a(full_adder_7_s), .b(and_7_out), .Cin(full_adder_11_cout), .S(P11), .Cout(full_adder_8_cout));
  full_adder full_adder_9 (
    .a(full_adder_12_cout), .b(and_8_out), .Cin(full_adder_13_cout), .S(full_adder_9_s),
    .Cout(full_adder_9_cout));
  full_adder full_adder_10 (
    .a(full_adder_9_s), .b(and_9_out), .Cin(full_adder_14_cout), .S(full_adder_10_s),
    .Cout(full_adder_10_cout));
  and and_11 (and_11_out, A3, B7);
  and and_12 (and_12_out, A7, B3);
  and and_13 (and_13_out, A5, B5);
  and and_14 (and_14_out, A4, B6);
  full_adder full_adder_11 (
    .a(full_adder_15_s), .b(and_11_out), .Cin(full_adder_16_cout), .S(P10), .Cout(full_adder_11_cout));
  full_adder full_adder_12 (
    .a(full_adder_17_cout), .b(and_12_out), .Cin(full_adder_18_cout), .S(full_adder_12_s),
    .Cout(full_adder_12_cout));
  and and_15 (and_15_out, A6, B4);
  full_adder full_adder_13 (
    .a(full_adder_12_s), .b(and_15_out), .Cin(full_adder_19_cout), .S(full_adder_13_s),
    .Cout(full_adder_13_cout));
  full_adder full_adder_14 (
    .a(full_adder_13_s), .b(and_13_out), .Cin(full_adder_20_cout), .S(full_adder_14_s),
    .Cout(full_adder_14_cout));
  full_adder full_adder_15 (
    .a(full_adder_14_s), .b(and_14_out), .Cin(full_adder_21_cout), .S(full_adder_15_s),
    .Cout(full_adder_15_cout));
  and and_16 (and_16_out, A2, B7);
  and and_17 (and_17_out, A4, B5);
  and and_18 (and_18_out, A3, B6);
  full_adder full_adder_16 (
    .a(full_adder_21_s), .b(and_16_out), .Cin(full_adder_25_cout), .S(P9), .Cout(full_adder_16_cout));
  and and_19 (and_19_out, A7, B2);
  full_adder full_adder_17 (
    .a(half_adder_1_cout), .b(and_19_out), .Cin(full_adder_26_cout), .S(full_adder_17_s),
    .Cout(full_adder_17_cout));
  and and_20 (and_20_out, A6, B3);
  full_adder full_adder_18 (
    .a(full_adder_17_s), .b(and_20_out), .Cin(full_adder_22_cout), .S(full_adder_18_s),
    .Cout(full_adder_18_cout));
  and and_21 (and_21_out, A5, B4);
  full_adder full_adder_19 (
    .a(full_adder_18_s), .b(and_21_out), .Cin(full_adder_27_cout), .S(full_adder_19_s),
    .Cout(full_adder_19_cout));
  full_adder full_adder_20 (
    .a(full_adder_19_s), .b(and_17_out), .Cin(full_adder_23_cout), .S(full_adder_20_s),
    .Cout(full_adder_20_cout));
  full_adder full_adder_21 (
    .a(full_adder_20_s), .b(and_18_out), .Cin(full_adder_24_cout), .S(full_adder_21_s),
    .Cout(full_adder_21_cout));
  and and_22 (and_22_out, A7, B1);
  half_adder half_adder_1 (.A(full_adder_28_cout), .B(and_22_out), .S(half_adder_1_s), .Cout(half_adder_1_cout));
  and and_23 (and_23_out, A3, B5);
  and and_24 (and_24_out, A2, B6);
  and and_25 (and_25_out, A1, B7);
  and and_26 (and_26_out, A6, B2);
  and and_27 (and_27_out, A5, B3);
  full_adder full_adder_22 (
    .a(full_adder_26_s), .b(and_27_out), .Cin(full_adder_32_cout), .S(full_adder_22_s),
    .Cout(full_adder_22_cout));
  and and_28 (and_28_out, A4, B4);
  full_adder full_adder_23 (
    .a(full_adder_27_s), .b(and_23_out), .Cin(full_adder_29_cout), .S(full_adder_23_s),
    .Cout(full_adder_23_cout));
  full_adder full_adder_24 (
    .a(full_adder_23_s), .b(and_24_out), .Cin(full_adder_30_cout), .S(full_adder_24_s),
    .Cout(full_adder_24_cout));
  full_adder full_adder_25 (
    .a(full_adder_24_s), .b(and_25_out), .Cin(half_adder_2_cout), .S(P8), .Cout(full_adder_25_cout));
  and and_29 (and_29_out, A7, B0);
  and and_30 (and_30_out, A6, B1);
  full_adder full_adder_26 (
    .a(half_adder_1_s), .b(and_26_out), .Cin(full_adder_31_cout), .S(full_adder_26_s),
    .Cout(full_adder_26_cout));
  full_adder full_adder_27 (
    .a(full_adder_22_s), .b(and_28_out), .Cin(full_adder_33_cout), .S(full_adder_27_s),
    .Cout(full_adder_27_cout));
  and and_31 (and_31_out, A2, B5);
  and and_32 (and_32_out, A1, B6);
  half_adder half_adder_2 (.A(and_36_out), .B(full_adder_30_s), .S(P7), .Cout(half_adder_2_cout));
  full_adder full_adder_28 (
    .a(and_29_out), .b(and_30_out), .Cin(full_adder_34_cout), .S(full_adder_28_s), .Cout(full_adder_28_cout));
  and and_33 (and_33_out, A5, B2);
  and and_34 (and_34_out, A4, B3);
  and and_35 (and_35_out, A3, B4);
  full_adder full_adder_29 (
    .a(full_adder_33_s), .b(and_31_out), .Cin(full_adder_38_cout), .S(full_adder_29_s),
    .Cout(full_adder_29_cout));
  full_adder full_adder_30 (
    .a(full_adder_29_s), .b(and_32_out), .Cin(half_adder_3_cout), .S(full_adder_30_s),
    .Cout(full_adder_30_cout));
  and and_36 (and_36_out, A0, B7);
  and and_37 (and_37_out, A6, B0);
  and and_38 (and_38_out, A5, B1);
  full_adder full_adder_31 (
    .a(full_adder_28_s), .b(and_33_out), .Cin(full_adder_35_cout), .S(full_adder_31_s),
    .Cout(full_adder_31_cout));
  full_adder full_adder_32 (
    .a(full_adder_31_s), .b(and_34_out), .Cin(full_adder_36_cout), .S(full_adder_32_s),
    .Cout(full_adder_32_cout));
  full_adder full_adder_33 (
    .a(full_adder_32_s), .b(and_35_out), .Cin(full_adder_37_cout), .S(full_adder_33_s),
    .Cout(full_adder_33_cout));
  full_adder full_adder_34 (
    .a(and_37_out), .b(and_38_out), .Cin(full_adder_39_cout), .S(full_adder_34_s), .Cout(full_adder_34_cout));
  and and_39 (and_39_out, A4, B2);
  and and_40 (and_40_out, A3, B3);
  and and_41 (and_41_out, A2, B4);
  and and_42 (and_42_out, A1, B5);
  half_adder half_adder_3 (.A(and_44_out), .B(full_adder_38_s), .S(P6), .Cout(half_adder_3_cout));
  and and_43 (and_43_out, A4, B1);
  full_adder full_adder_35 (
    .a(full_adder_34_s), .b(and_39_out), .Cin(full_adder_40_cout), .S(full_adder_35_s),
    .Cout(full_adder_35_cout));
  full_adder full_adder_36 (
    .a(full_adder_35_s), .b(and_40_out), .Cin(full_adder_41_cout), .S(full_adder_36_s),
    .Cout(full_adder_36_cout));
  full_adder full_adder_37 (
    .a(full_adder_36_s), .b(and_41_out), .Cin(full_adder_42_cout), .S(full_adder_37_s),
    .Cout(full_adder_37_cout));
  full_adder full_adder_38 (
    .a(full_adder_37_s), .b(and_42_out), .Cin(half_adder_4_cout), .S(full_adder_38_s),
    .Cout(full_adder_38_cout));
  and and_44 (and_44_out, A0, B6);
  and and_45 (and_45_out, B0, A5);
  full_adder full_adder_39 (
    .a(and_45_out), .b(and_43_out), .Cin(full_adder_43_cout), .S(full_adder_39_s), .Cout(full_adder_39_cout));
  and and_46 (and_46_out, A3, B2);
  and and_47 (and_47_out, A2, B3);
  and and_48 (and_48_out, A1, B4);
  half_adder half_adder_4 (.A(and_50_out), .B(full_adder_42_s), .S(P5), .Cout(half_adder_4_cout));
  and and_49 (and_49_out, A3, B1);
  full_adder full_adder_40 (
    .a(full_adder_39_s), .b(and_46_out), .Cin(full_adder_44_cout), .S(full_adder_40_s),
    .Cout(full_adder_40_cout));
  full_adder full_adder_41 (
    .a(full_adder_40_s), .b(and_47_out), .Cin(full_adder_45_cout), .S(full_adder_41_s),
    .Cout(full_adder_41_cout));
  full_adder full_adder_42 (
    .a(full_adder_41_s), .b(and_48_out), .Cin(half_adder_5_cout), .S(full_adder_42_s),
    .Cout(full_adder_42_cout));
  and and_50 (and_50_out, A0, B5);
  and and_51 (and_51_out, B0, A4);
  full_adder full_adder_43 (
    .a(and_51_out), .b(and_49_out), .Cin(full_adder_46_cout), .S(full_adder_43_s), .Cout(full_adder_43_cout));
  and and_52 (and_52_out, A2, B2);
  and and_53 (and_53_out, A1, B3);
  and and_54 (and_54_out, A2, B1);
  full_adder full_adder_44 (
    .a(full_adder_43_s), .b(and_52_out), .Cin(full_adder_47_cout), .S(full_adder_44_s),
    .Cout(full_adder_44_cout));
  full_adder full_adder_45 (
    .a(full_adder_44_s), .b(and_53_out), .Cin(half_adder_6_cout), .S(full_adder_45_s),
    .Cout(full_adder_45_cout));
  half_adder half_adder_5 (.A(and_56_out), .B(full_adder_45_s), .S(P4), .Cout(half_adder_5_cout));
  and and_55 (and_55_out, A3, B0);
  full_adder full_adder_46 (
    .a(and_55_out), .b(and_54_out), .Cin(full_adder_48_cout), .S(full_adder_46_s), .Cout(full_adder_46_cout));
  and and_56 (and_56_out, A0, B4);
  and and_57 (and_57_out, A1, B2);
  full_adder full_adder_47 (
    .a(full_adder_46_s), .b(and_57_out), .Cin(half_adder_7_cout), .S(full_adder_47_s),
    .Cout(full_adder_47_cout));
  half_adder half_adder_6 (.A(and_59_out), .B(full_adder_47_s), .S(P3), .Cout(half_adder_6_cout));
  and and_58 (and_58_out, A1, B1);
  and and_59 (and_59_out, A0, B3);
  and and_60 (and_60_out, A2, B0);
  full_adder full_adder_48 (
    .a(and_60_out), .b(and_58_out), .Cin(half_adder_8_cout), .S(full_adder_48_s), .Cout(full_adder_48_cout));
  half_adder half_adder_7 (.A(and_62_out), .B(full_adder_48_s), .S(P2), .Cout(half_adder_7_cout));
  and and_61 (and_61_out, A0, B1);
  and and_62 (and_62_out, A0, B2);
  and and_63 (and_63_out, B0, A1);
  half_adder half_adder_8 (.A(and_63_out), .B(and_61_out), .S(P1), .Cout(half_adder_8_cout));
  and and_64 (P0, B0, A0);

  // Other names for the same wires on the sheet: A0_t = A0; A1_t = A1; A2_t = A2; A3_t = A3; A4_t = A4; A5_t = A5;
  //   A6_t = A6; A7_t = A7; B0_t = B0; B1_t = B1; B2_t = B2; B3_t = B3; B4_t = B4; B5_t = B5; B6_t = B6; B7_t = B7
endmodule
